// Logisim project star.circ as structural Verilog: 1 circuit, main circuit main
module main (
);

  wire clock_1_out, d_ff_1_q, d_ff_2_q, d_ff_3_q, d_ff_4_q, d_ff_4_qn;

  LED led_1 (.in(d_ff_3_q));
  LED led_2 (.in(d_ff_3_q));
  LED led_3 (.in(d_ff_3_q));
  LED led_4 (.in(d_ff_2_q));
  LED led_5 (.in(d_ff_2_q));
  LED led_6 (.in(d_ff_3_q));
  Clock clock_1 (.out(clock_1_out));
  LED led_7 (.in(d_ff_3_q));
  LED led_8 (.in(d_ff_3_q));
  LED led_9 (.in(d_ff_3_q));
  LED led_10 (.in(d_ff_2_q));
  LED led_11 (.in(d_ff_1_q));
  LED led_12 (.in(d_ff_2_q));
  LED led_13 (.in(d_ff_3_q));
  LED led_14 (.in(d_ff_3_q));
  LED led_15 (.in(d_ff_3_q));
  D_Flip_Flop d_ff_1 (.D(d_ff_4_qn), .clk(clock_1_out), .Q(d_ff_1_q));  // open: Qn, preset, reset
  LED led_16 (.in(d_ff_2_q));
  LED led_17 (.in(d_ff_2_q));
  LED led_18 (.in(d_ff_1_q));
  LED led_19 (.in(d_ff_2_q));
  LED led_20 (.in(d_ff_1_q));
  LED led_21 (.in(d_ff_1_q));
  LED led_22 (.in(d_ff_1_q));
  LED led_23 (.in(d_ff_2_q));
  LED led_24 (.in(d_ff_1_q));
  LED led_25 (.in(d_ff_2_q));
  LED led_26 (.in(d_ff_1_q));
  LED led_27 (.in(d_ff_2_q));
  D_Flip_Flop d_ff_2 (.D(d_ff_1_q), .clk(clock_1_out), .Q(d_ff_2_q));  // open: Qn, preset, reset
  LED led_28 (.in(d_ff_2_q));
  LED led_29 (.in(d_ff_2_q));
  LED led_30 (.in(d_ff_2_q));
  LED led_31 (.in(d_ff_1_q));
  LED led_32 (.in(d_ff_2_q));
  LED led_33 (.in(d_ff_2_q));
  LED led_34 (.in(d_ff_2_q));
  LED led_35 (.in(d_ff_3_q));
  LED led_36 (.in(d_ff_3_q));
  LED led_37 (.in(d_ff_3_q));
  LED led_38 (.in(d_ff_2_q));
  LED led_39 (.in(d_ff_1_q));
  LED led_40 (.in(d_ff_2_q));
  LED led_41 (.in(d_ff_3_q));
  LED led_42 (.in(d_ff_3_q));
  LED led_43 (.in(d_ff_3_q));
  D_Flip_Flop d_ff_3 (.D(d_ff_2_q), .clk(clock_1_out), .Q(d_ff_3_q));  // open: Qn, preset, reset
  LED led_44 (.in(d_ff_3_q));
  LED led_45 (.in(d_ff_3_q));
  LED led_46 (.in(d_ff_2_q));
  LED led_47 (.in(d_ff_2_q));
  LED led_48 (.in(d_ff_3_q));
  LED led_49 (.in(d_ff_3_q));
  D_Flip_Flop d_ff_4 (.D(d_ff_3_q), .clk(clock_1_out), .Q(d_ff_4_q), .Qn(d_ff_4_qn));  // open: preset, reset
endmodule
